# Fritzing sketch sktech (saved by Fritzing 0.9.4)
circuit board: 8.46667cm x 5.64444cm
perfboards: 1

parts:
  Arduino_Nano = Arduino Nano (Rev3.0)
  FAN1 = male pin header, 4 pins [form="♂ (male)"]
  12V_DC_5521 = Power plug
  10K_Ohm_R1 = Resistor [tolerance=±5% resistance=10k package=THT]
  LCM1602_I2C = LCM1602 IIC [part_number="LCM1602 IIC" chip_label="LCM1602 IIC" package="DIP (Dual Inline) [THT]"]
  J1 = male pin header, 4 pins [form="♂ (male)"]
  LCD1602 = LCD screen

nets:
  N1: Arduino_Nano.D2, FAN1.pin2, 10K_Ohm_R1.Pin_1
  N2: Arduino_Nano.D3, FAN1.pin1
  5V: Arduino_Nano.5V, 10K_Ohm_R1.Pin_0, LCM1602_I2C.VCC, J1.pin3
  N3: Arduino_Nano.A5, LCM1602_I2C.SCL, J1.pin1
  N4: Arduino_Nano.A4, LCM1602_I2C.SDA, J1.pin2
  N5: FAN1.pin3, 12V_DC_5521.VCC
  N6: FAN1.pin4, 12V_DC_5521.GND
  VSS: LCM1602_I2C.VSS, LCD1602.VSS
  VDD: LCM1602_I2C.VDD, LCD1602.VDD
  N7: LCM1602_I2C.V0, LCD1602.V0
  N8: LCM1602_I2C.RS, LCD1602.RS
  N9: LCM1602_I2C.RW, LCD1602.R/W
  N10: LCM1602_I2C.E, LCD1602.E
  N11: LCM1602_I2C.D0, LCD1602.DB0
  N12: LCM1602_I2C.D1, LCD1602.DB1
  N13: LCM1602_I2C.D2, LCD1602.DB2
  N14: LCM1602_I2C.D3, LCD1602.DB3
  N15: LCM1602_I2C.D4, LCD1602.DB4
  N16: LCM1602_I2C.D5, LCD1602.DB5
  N17: LCM1602_I2C.D6, LCD1602.DB6
  N18: LCM1602_I2C.D7, LCD1602.DB7
  N19: LCM1602_I2C.A, LCD1602.LED+
  N20: LCM1602_I2C.K, LCD1602.LED-
  N21: LCM1602_I2C.GND, J1.pin4
  N22: LCM1602_I2C.LED_A, LCM1602_I2C.LED_B

custom parts:
  LCM1602 IIC: I2C-Module to use a 1602 or 2004 LCD on with the wire.h libory Serial LCD Modul
